# Fritzing sketch Часть с ардуинкой(модель в Fritzing) (saved by Fritzing 0.9.5d)

parts:
  Компонент1 = Arduino Nano (Rev3.0)
  M1 = BF [package=THT]

nets:
  N1: Компонент1.D2, M1.pin1
  N2: Компонент1.GND, M1.pin3
  N3: Компонент1.5V, M1.pin2

notes:
  Тензодатчик BF350-3AA, внедряется в эспандер
  Arduino Nano, подключается к компьютеру
  Питание всей схемы и передача данных на компьютер идет через USB на Arduino

custom parts:
  : BF350-3AA SainSmart Strain gauge Bending detection Test Sensor Module Weigh Amplifier Voltage Output
